# Fritzing sketch LampSchematic (saved by Fritzing 0.9.10b)
breadboards: 1

parts:
  M5Stack-ATOM-Matrix1 = atom-matrix [package=M5Stack]
  R1 = Resistor [tolerance=±5% power=0.25 resistance=220 package=THT]
  R2 = Resistor [tolerance=±5% power=0.25 resistance=220 package=THT]
  R3 = Resistor [tolerance=±5% power=0.25 resistance=220 package=THT]
  R4 = Resistor [tolerance=±5% power=0.25 resistance=220 package=THT]
  LED1 = LED - 5mm [color="Red (633nm)" current=0.030 package="5 mm [THT]"]
  LED2 = LED - 5mm [color="Green (560nm)" current=0.030 package="5 mm [THT]"]
  LED3 = LED - 5mm [color="Blue (430nm)" current=0.030 package="5 mm [THT]"]
  LED4 = LED - 5mm [color="White (4500K)" current=0.030 package="5 mm [THT]"]
  S1 = Pushbutton [package="[THT]"]
  NEOPIXEL1 = Neopixel Strip -- White (30/m)
  Angle_Sensor1 = Angle Sensor  # not connected

nets:
  N1: M5Stack-ATOM-Matrix1.G21, S1.Pin_3, S1.Pin_4
  N2: M5Stack-ATOM-Matrix1.G26, NEOPIXEL1.Din
  N3: M5Stack-ATOM-Matrix1.5Vb, NEOPIXEL1.+5V
  N4: M5Stack-ATOM-Matrix1.GNDb, LED1.cathode, LED2.cathode, LED3.cathode, LED4.cathode, S1.Pin_1, S1.Pin_2, NEOPIXEL1.GND
  N5: M5Stack-ATOM-Matrix1.G33, R1.Pin_0
  N6: M5Stack-ATOM-Matrix1.G23, R2.Pin_0
  N7: M5Stack-ATOM-Matrix1.G19, R3.Pin_0
  N8: M5Stack-ATOM-Matrix1.G22, R4.Pin_0
  N9: R1.Pin_1, LED1.anode
  N10: R2.Pin_1, LED2.anode
  N11: R3.Pin_1, LED3.anode
  N12: R4.Pin_1, LED4.anode

custom parts:
  atom-matrix: M5Stack ATOM Matrix
  Neopixel Strip -- White (30/m): These NeoPixel strips have 30 digitally-addressable pixel LEDs per meter and are very affordable and are only 12.5 mm wide, 10 mm if you remove the strip from the casing.
  Angle Sensor: The Angle sensor is a simple potentiometer which changes the resistance in the circuit when twisted
