# Fritzing sketch QuarterCircuit (saved by Fritzing 0.9.10b)
breadboards: 1

parts:
  M5Stack-ATOM-Matrix1 = atom-matrix [package=M5Stack]
  LED1 = LED - 5mm [color="Red (633nm)" current=0.030 package="5 mm [THT]"]
  LED2 = LED - 5mm [color="Green (555nm)" current=0.030 package="5 mm [THT]"]
  R1 = Resistor [tolerance=±5% power=0.25 resistance=220 package=THT]
  R2 = Resistor [tolerance=±5% power=0.25 resistance=220 package=THT]
  Button_(Quarters) = Pushbutton [package=THT]

nets:
  GND/copper tape/quarter: M5Stack-ATOM-Matrix1.G25, M5Stack-ATOM-Matrix1.G32, M5Stack-ATOM-Matrix1.G26, M5Stack-ATOM-Matrix1.GNDb, LED1.cathode, LED1.anode, LED2.cathode, LED2.anode, R1.Pin_0, R1.Pin_1, R2.Pin_0, R2.Pin_1, Button_(Quarters).leg0, Button_(Quarters).leg1

custom parts:
  atom-matrix: M5Stack ATOM Matrix
